# Fritzing sketch control-plate-without-leds (saved by Fritzing 0.9.3b)
breadboards: 1

parts:
  S1 = Pushbutton [package="[THT]"]
  S2 = Pushbutton [package="[THT]"]
  S3 = Pushbutton [package="[THT]"]
  S4 = Pushbutton [package="[THT]"]
  S5 = Pushbutton [package="[THT]"]
  S6 = Pushbutton [package="[THT]"]
  D1 = Diode [package=sma-diode_alt]
  D2 = Diode [package=sma-diode_alt]
  D3 = Diode [package=sma-diode_alt]
  J1 = shrouded pin header, 8 pins [form="♂ (shrouded male)"]

nets:
  N1: S1.Pin_1, S1.Pin_2, S2.Pin_3, S2.Pin_4, D3.C
  N2: S1.Pin_3, S1.Pin_4, S3.Pin_3, S3.Pin_4, S5.Pin_3, J1.pin7
  N3: S2.Pin_1, S2.Pin_2, S4.Pin_3, S4.Pin_4, S6.Pin_3, S6.Pin_4, J1.pin8
  N4: S3.Pin_1, S3.Pin_2, S4.Pin_1, D2.C
  N5: S5.Pin_1, S5.Pin_2, S6.Pin_1, S6.Pin_2, D1.C
  N6: D1.A, J1.pin1
  N7: D2.A, J1.pin2
  N8: D3.A, J1.pin3
